# Fritzing sketch esquemaDispositivo (saved by Fritzing 0.9.3b)
perfboards: 1

parts:
  J2 = Infrared Proximity Sensor  # not connected
  U2 = ESP8266 ESP-01 Upgraded WiFi Module [part_number=ESP8266]
  R1 = Resistor [tolerance=±5% resistance=330 package=THT]  # not connected
  VCC1 = Battery
  S1 = Pushbutton [package="[SMD]"]
  Q1 = TRANSISTOR_NPN [package=to-92]  # not connected
  J1 = Piezo Speaker  # not connected

nets:
  N1: U2.GND, VCC1.-
  N2: S1.Pin_1, S1.Pin_2
  N3: S1.Pin_3, S1.Pin_4

notes:
  Batería 4V
  Sensor de Distancia
  Buzzer

custom parts:
  ESP8266 ESP-01 Upgraded WiFi Module: Upgraded Version ESP-01,all Flash are upgraded to 1M byte.Also support Cloud service remote transmission.
